// Logisim project alu.circ as structural Verilog: 1 circuit, main circuit alu
module alu (
  input  [31:0] A,
  input  [31:0] B,
  input  [3:0] ALUSel,
  output [31:0] ALUResult
);

  wire comparator_1_lt;
  wire [4:0] bit_extender_5_out, bit_extender_6_out, bit_extender_7_out;
  wire [31:0] add0, and7, mul8, mulh9, mulhu11, multiplier_4_out, or6, sll1, slt2, sra13, srl5, sub12, xor4;
  wire [63:0] bit_extender_1_out, bit_extender_2_out, bit_extender_3_out, bit_extender_4_out,
       multiplier_2_out, multiplier_3_out, shifter_3_out, shifter_4_out;

  Multiplexer #(.enable("false"), .select(4), .width(32)) multiplexer_1 (
    .in0(add0), .in1(sll1), .in2(slt2), .in3(xor4), .in4(srl5), .in5(or6), .in6(and7), .in7(mul8),
    .in8(mulh9), .in9(mulhu11), .in10(sub12), .in11(sra13), .in12(B), .out(ALUResult), .sel(ALUSel));  // open: in13, in14, in15
  assign bit_extender_1_out = {{32{A[31]}}, A};  // Bit_Extender bit_extender_1
  assign bit_extender_2_out = {{32{B[31]}}, B};  // Bit_Extender bit_extender_2
  assign bit_extender_3_out = {{32{A[31]}}, A};  // Bit_Extender bit_extender_3
  assign bit_extender_4_out = {{32{B[31]}}, B};  // Bit_Extender bit_extender_4
  Adder #(.width(32)) adder_1 (.a(A), .b(B), .out(add0));  // open: cin, cout
  Bit_Extender #(.in_width(32), .out_width(5)) bit_extender_5 (.in(B), .out(bit_extender_5_out));
  Comparator #(.width(32)) comparator_1 (.a(A), .b(B), .lt(comparator_1_lt));  // open: gt, eq
  assign xor4 = A ^ B;  // XOR_Gate xor_1, 32 bits wide
  Bit_Extender #(.in_width(32), .out_width(5)) bit_extender_6 (.in(B), .out(bit_extender_6_out));
  assign or6 = A | B;  // OR_Gate or_1, 32 bits wide
  assign and7 = A & B;  // AND_Gate and_1, 32 bits wide
  Multiplier #(.mode("twosComplement"), .width(32)) multiplier_1 (.a(A), .b(B), .out(mul8));  // open: cin, cout
  Multiplier #(.mode("twosComplement"), .width(64)) multiplier_2 (
    .a(bit_extender_1_out), .b(bit_extender_2_out), .out(multiplier_2_out));  // open: cin, cout
  Multiplier #(.width(64)) multiplier_3 (
    .a(bit_extender_3_out), .b(bit_extender_4_out), .out(multiplier_3_out));  // open: cin, cout
  Adder #(.width(32)) adder_2 (.a(A), .b(multiplier_4_out), .out(sub12));  // open: cin, cout
  Multiplier #(.width(32)) multiplier_4 (.a({32{1'b1}}), .b(B), .out(multiplier_4_out));  // open: cin, cout
  Bit_Extender #(.in_width(32), .out_width(5)) bit_extender_7 (.in(B), .out(bit_extender_7_out));
  Shifter #(.width(32)) shifter_1 (.in(A), .\dist (bit_extender_5_out), .out(sll1));
  assign slt2 = {{31{comparator_1_lt}}, comparator_1_lt};  // Bit_Extender bit_extender_8
  Shifter #(.shift("lr"), .width(32)) shifter_2 (.in(A), .\dist (bit_extender_6_out), .out(srl5));
  Shifter #(.shift("lr"), .width(64)) shifter_3 (.in(multiplier_2_out), .\dist (6'b100000), .out(shifter_3_out));
  Shifter #(.shift("lr"), .width(64)) shifter_4 (.in(multiplier_3_out), .\dist (6'b100000), .out(shifter_4_out));
  Shifter #(.shift("ar"), .width(32)) shifter_5 (.in(A), .\dist (bit_extender_7_out), .out(sra13));
  Bit_Extender #(.in_width(64), .out_width(32)) bit_extender_9 (.in(shifter_3_out), .out(mulh9));
  Bit_Extender #(.in_width(64), .out_width(32)) bit_extender_10 (.in(shifter_4_out), .out(mulhu11));

  // Other names for the same wires on the sheet: bsel15[31:0] = B

  // Notes on the sheet:
  //   INPUTS to your circuit
  //   DON'T CHANGE THE LOCATIONS OF THE INPUTS AND OUTPUTS!
  //   OUTPUT from your circuit
endmodule
