// Logisim project cpu.circ as structural Verilog: 1 circuit, main circuit cpu
module cpu (
  input  clk,
  input  [31:0] Instruction,
  input  [31:0] MemReadData,
  output [31:0] MemAddress,
  output [31:0] ProgramCounter,
  output [31:0] ra,
  output [31:0] sp,
  output [31:0] t0,
  output [31:0] t1,
  output [31:0] t2,
  output [31:0] s0,
  output [31:0] s1,
  output [31:0] a0,
  output [3:0] MemWriteMask,
  output [31:0] MemWriteData
);

  wire BrEq, BrLt, BrUn, MemWEn, RegWEn;
  wire [2:0] immSel;
  wire [3:0] ALUSel;
  wire [4:0] branch_store_dest, destReg, S_format_dest, undriven, undriven_3, undriven_4, undriven_5,
       undriven_6, undriven_7, undriven_8, undriven_9, undriven_10, undriven_11, undriven_12, undriven_13,
       undriven_14, undriven_15, undriven_16, undriven_17, undriven_18, undriven_19, undriven_20,
       undriven_21, undriven_22, undriven_23, undriven_24;
  wire [31:0] adder_1_out, B, branch_store, I_imm_math, I_load, J_jal, J_jalr, partial_store_1_datatomem,
       readReg1, RegWriteData, U_auipc, U_lui, undriven_2, val1, val2, val3, val6, val7, val9, val10, val11,
       val14, val15, val16, val17, val18, val19, val20, val21, val22, val23, val26, val28, val29, val30,
       val31;

  Register #(.width(32)) PC (.D(adder_1_out), .clk(clk), .Q(ProgramCounter));  // open: en, clr
  Adder #(.width(32)) adder_1 (.a(ProgramCounter), .b(32'h4), .out(adder_1_out));  // open: cin, cout
  assign ALUSel = {{1{1'b0}}, Instruction[14:12]};  // Bit_Extender bit_extender_1
  control_logic control_logic_1 (
    .RegWEn(RegWEn), .ImmSel(immSel), .BrUn(BrUn), .ALUSel(ALUSel), .MemWEn(MemWEn),
    .Instruction(Instruction), .BrEq(BrEq), .BrLt(BrLt));  // open: PCSel, ASel, BSel, WBSel
  regfile regfile_1 (
    .ReadReg1(Instruction[19:15]), .ReadReg2(Instruction[24:20]), .WriteReg(destReg),
    .RegWriteData(RegWriteData), .RegWEn(RegWEn), .clk(clk), .ra(ra), .sp(sp), .t0(t0), .t1(t1), .t2(t2),
    .s0(s0), .s1(s1), .a0(a0), .RegReadData1(readReg1), .RegReadData2(branch_store));
  imm_gen imm_gen_1 (.Instruction(Instruction), .ImmSel(immSel), .Immediate(I_imm_math));
  Multiplexer #(.enable("false"), .select(5), .width(32)) multiplexer_1 (
    .in0(I_load), .in1(val1), .in2(val2), .in3(val3), .in4(I_imm_math), .in5(U_auipc), .in6(val6),
    .in7(val7), .in8(branch_store), .in9(val9), .in10(val10), .in11(val11), .in12(branch_store),
    .in13(U_lui), .in14(val14), .in15(val15), .in16(val16), .in17(val17), .in18(val18), .in19(val19),
    .in20(val20), .in21(val21), .in22(val22), .in23(val23), .in24(branch_store), .in25(J_jalr), .in26(val26),
    .in27(J_jal), .in28(val28), .in29(val29), .in30(val30), .in31(val31), .out(B), .sel(Instruction[6:2]));
  alu alu_1 (.ALUResult(RegWriteData), .A(readReg1), .B(B), .ALUSel(ALUSel));
  branch_comp branch_comp_1 (.BrUn(BrUn), .BrEq(BrEq), .BrLt(BrLt));  // open: BrData1, BrData2
  Multiplexer #(.enable("false"), .select(5), .width(5)) multiplexer_2 (
    .in0(Instruction[11:7]), .in1(undriven), .in2(undriven_3), .in3(undriven_4), .in4(Instruction[11:7]),
    .in5(Instruction[11:7]), .in6(undriven_5), .in7(undriven_6), .in8(S_format_dest), .in9(undriven_7),
    .in10(undriven_8), .in11(undriven_9), .in12(Instruction[11:7]), .in13(Instruction[11:7]),
    .in14(undriven_10), .in15(undriven_11), .in16(undriven_12), .in17(undriven_13), .in18(undriven_14),
    .in19(undriven_15), .in20(undriven_16), .in21(undriven_17), .in22(undriven_18), .in23(undriven_19),
    .in24(branch_store_dest), .in25(Instruction[11:7]), .in26(undriven_20), .in27(Instruction[11:7]),
    .in28(undriven_21), .in29(undriven_22), .in30(undriven_23), .in31(undriven_24), .out(destReg),
    .sel(Instruction[6:2]));
  partial_store partial_store_1 (
    .Instruction(Instruction), .MemAddress(MemAddress), .DataFromReg(undriven_2), .MemWEn(MemWEn),
    .MemWriteMask(MemWriteMask), .DataToMem(partial_store_1_datatomem));
  partial_load partial_load_1 (.Instruction(Instruction), .MemAddress(MemAddress));  // open: DataFromMem, DataToReg

  // Other names for the same wires on the sheet: funct3[2:0] = Instruction[14:12]; imm19_12[7:0] = Instruction[19:12];
  //   imm31_12[10:0] = {Instruction[31:22], Instruction[12]}; imm20 = Instruction[20];
  //   imm31_20[11:0] = Instruction[31:20]; rs2[4:0] = Instruction[24:20]; imm30_21[9:0] = Instruction[30:21];
  //   funct7[6:0] = Instruction[31:25]; imm30_25[5:0] = Instruction[30:25]; imm31_25[6:0] = Instruction[31:25];
  //   imm31 = Instruction[31]; I_imm_math_dest[4:0] = Instruction[11:7]; I_load_dest[4:0] = Instruction[11:7];
  //   imm7 = Instruction[7]; imm11_7[4:0] = Instruction[11:7]; J_jal_dest[4:0] = Instruction[11:7];
  //   J_jalr_dest[4:0] = Instruction[11:7]; R_format_dest[4:0] = Instruction[11:7]; rd[4:0] = Instruction[11:7];
  //   U_auipc_dest[4:0] = Instruction[11:7]; U_lui_dest[4:0] = Instruction[11:7]; imm11_8[3:0] = Instruction[11:8];
  //   rs1[4:0] = Instruction[19:15]; opcode[4:0] = Instruction[6:2]; R_format[31:0] = branch_store;
  //   readReg2[31:0] = branch_store; S_format[31:0] = branch_store

  // Notes on the sheet:
  //   To IMEM
  //   IMEM (do **NOT** move this)
  //   From IMEM
  //   opcode
  //   funct3 (might have a problem being undefined)
  //   These determine what values go to A, B
  //   Need to determine B for non I, R, S, Branch 
  //   Inputs/Outputs for testing. Do **NOT** move these.
  //   It is OK to move the PC, RegFile, ALU, MEM, Branch Comp, Imm Gen, Partial Load, Partial Store and Control Logic to wherever is most convenient for you when constructing your CPU, and to delete this text
  //   always a register read value
  //   either a register read value or an immediate
  //   Opcodes:
  //   S-Format = 8
  //   R-Format: 12
  //   Branch / Store = 24
  //   J-Format --> jal: 27; jalr: 25
  //   U-Format --> lui = 13; auipc = 5
  //   I-Type --> immediate log/arith = 4; load = 0
  //   These determine what the return register is
  //   still need to put RD for S, Branch
  //   To DMEM
  //   Opcodes:
  //   R-Format: 12
  //   S-Format = 8
  //   DMEM (do **NOT** move this)
  //   I-Type --> immediate log/arith = 4; load = 0
  //   Branch / Store = 24
  //   J-Format --> jal: 27; jalr: 25
  //   U-Format --> lui = 13; auipc = 5
  //   From DMEM
endmodule
